// Logisim project control-logic.circ as structural Verilog: 1 circuit, main circuit control_logic
module control_logic (
  input  [31:0] Instruction,
  input  BrEq,
  input  BrLt,
  output PCSel,
  output RegWEn,
  output [2:0] ImmSel,
  output BrUn,
  output ASel,
  output BSel,
  output [3:0] ALUSel,
  output MemWEn,
  output [1:0] WBSel,
  output [5:0] out_13
);

  wire and_34_out, and_35_out, and_36_out, and_37_out, and_38_out, and_39_out, comparator_1_eq,
       comparator_2_eq, comparator_3_eq, comparator_4_eq, comparator_5_eq, comparator_6_eq, comparator_7_eq,
       comparator_8_eq, comparator_9_eq, comparator_10_eq, comparator_11_eq, comparator_12_eq,
       comparator_13_eq, comparator_14_eq, comparator_15_eq, comparator_16_eq, comparator_17_eq,
       comparator_18_eq, comparator_19_eq, comparator_20_eq, comparator_21_eq, comparator_22_eq,
       comparator_23_eq, comparator_24_eq, comparator_25_eq, comparator_26_eq, comparator_27_eq,
       comparator_28_eq, comparator_29_eq, comparator_30_eq, comparator_31_eq, comparator_32_eq,
       comparator_33_eq, comparator_34_eq, comparator_35_eq, comparator_36_eq, comparator_37_eq,
       comparator_38_eq, comparator_39_eq, comparator_40_eq, comparator_41_eq, comparator_42_eq,
       comparator_43_eq, comparator_44_eq, comparator_45_eq, comparator_46_eq, comparator_47_eq,
       comparator_48_eq, comparator_49_eq, comparator_50_eq, comparator_51_eq, comparator_52_eq,
       comparator_53_eq, comparator_54_eq, comparator_55_eq, comparator_56_eq, comparator_57_eq,
       comparator_58_eq, comparator_59_eq, comparator_60_eq, comparator_61_eq, comparator_62_eq,
       comparator_63_eq, comparator_64_eq, comparator_65_eq, comparator_66_eq, comparator_67_eq,
       comparator_68_eq, comparator_69_eq, comparator_70_eq, comparator_71_eq, comparator_72_eq,
       comparator_73_eq, comparator_74_eq, comparator_75_eq, comparator_76_eq, comparator_77_eq,
       comparator_78_eq, comparator_79_eq, comparator_83_eq, comparator_84_eq, is_add, is_addi, is_and,
       is_andi, is_auipc, is_beq, is_bge, is_bgeu, is_blt, is_bltu, is_bne, is_jal, is_jalr, is_lb, is_lh,
       is_lui, is_lw, is_mul, is_mulh, is_mulhu, is_or, is_ori, is_sb, is_sh, is_sll, is_slli, is_slt,
       is_slti, is_sra, is_srai, is_srl, is_srli, is_sub, is_sw, is_xor, is_xori, not_1_out, not_2_out,
       not_3_out, priority_encoder_1_gs, priority_encoder_2_gs, priority_encoder_3_gs;
  wire [1:0] priority_encoder_3_out;
  wire [3:0] multiplexer_1_out, priority_encoder_1_out, priority_encoder_2_out;
  wire [5:0] adder_1_out, adder_2_out, adder_3_out, bit_extender_1_out, bit_extender_2_out,
       bit_extender_3_out, multiplexer_2_out, multiplexer_3_out;
  wire [15:14] rom_1_data;

  ROM #(.addrWidth(6), .dataWidth(16)) rom_1 (
    .addr(out_13), .data({rom_1_data, WBSel, MemWEn, ALUSel, BSel, ASel, BrUn, ImmSel, RegWEn}));
  Comparator #(.width(7)) comparator_1 (.a(Instruction[6:0]), .b(7'b0110011), .eq(comparator_1_eq));  // open: gt, lt
  Comparator #(.width(3)) comparator_2 (.a(Instruction[14:12]), .b(3'b000), .eq(comparator_2_eq));  // open: gt, lt
  Comparator #(.width(7)) comparator_3 (.a(Instruction[31:25]), .b({7{1'b0}}), .eq(comparator_3_eq));  // open: gt, lt
  Comparator #(.width(7)) comparator_4 (.a(Instruction[6:0]), .b(7'b0110011), .eq(comparator_4_eq));  // open: gt, lt
  Comparator #(.width(3)) comparator_5 (.a(Instruction[14:12]), .b(3'b000), .eq(comparator_5_eq));  // open: gt, lt
  Comparator #(.width(7)) comparator_6 (.a(Instruction[31:25]), .b(7'b0000001), .eq(comparator_6_eq));  // open: gt, lt
  Comparator #(.width(7)) comparator_7 (.a(Instruction[6:0]), .b(7'b0110011), .eq(comparator_7_eq));  // open: gt, lt
  Comparator #(.width(3)) comparator_8 (.a(Instruction[14:12]), .b(3'b000), .eq(comparator_8_eq));  // open: gt, lt
  Comparator #(.width(7)) comparator_9 (.a(Instruction[31:25]), .b(7'b0100000), .eq(comparator_9_eq));  // open: gt, lt
  Comparator #(.width(7)) comparator_10 (.a(Instruction[6:0]), .b(7'b0110011), .eq(comparator_10_eq));  // open: gt, lt
  Comparator #(.width(3)) comparator_11 (.a(Instruction[14:12]), .b(3'b001), .eq(comparator_11_eq));  // open: gt, lt
  Comparator #(.width(7)) comparator_12 (.a(Instruction[31:25]), .b({7{1'b0}}), .eq(comparator_12_eq));  // open: gt, lt
  Comparator #(.width(7)) comparator_13 (.a(Instruction[6:0]), .b(7'b0110011), .eq(comparator_13_eq));  // open: gt, lt
  Comparator #(.width(3)) comparator_14 (.a(Instruction[14:12]), .b(3'b001), .eq(comparator_14_eq));  // open: gt, lt
  Comparator #(.width(7)) comparator_15 (
    .a(Instruction[31:25]), .b(7'b0000001), .eq(comparator_15_eq));  // open: gt, lt
  Comparator #(.width(7)) comparator_16 (.a(Instruction[6:0]), .b(7'b0110011), .eq(comparator_16_eq));  // open: gt, lt
  Comparator #(.width(3)) comparator_17 (.a(Instruction[14:12]), .b(3'b011), .eq(comparator_17_eq));  // open: gt, lt
  Comparator #(.width(7)) comparator_18 (
    .a(Instruction[31:25]), .b(7'b0000001), .eq(comparator_18_eq));  // open: gt, lt
  Comparator #(.width(7)) comparator_19 (.a(Instruction[6:0]), .b(7'b0110011), .eq(comparator_19_eq));  // open: gt, lt
  Comparator #(.width(3)) comparator_20 (.a(Instruction[14:12]), .b(3'b010), .eq(comparator_20_eq));  // open: gt, lt
  Comparator #(.width(7)) comparator_21 (.a(Instruction[31:25]), .b({7{1'b0}}), .eq(comparator_21_eq));  // open: gt, lt
  Comparator #(.width(7)) comparator_22 (.a(Instruction[6:0]), .b(7'b0110011), .eq(comparator_22_eq));  // open: gt, lt
  Comparator #(.width(3)) comparator_23 (.a(Instruction[14:12]), .b(3'b100), .eq(comparator_23_eq));  // open: gt, lt
  Comparator #(.width(7)) comparator_24 (.a(Instruction[31:25]), .b({7{1'b0}}), .eq(comparator_24_eq));  // open: gt, lt
  Comparator #(.width(7)) comparator_25 (.a(Instruction[6:0]), .b(7'b0110011), .eq(comparator_25_eq));  // open: gt, lt
  Comparator #(.width(3)) comparator_26 (.a(Instruction[14:12]), .b(3'b101), .eq(comparator_26_eq));  // open: gt, lt
  Comparator #(.width(7)) comparator_27 (.a(Instruction[31:25]), .b({7{1'b0}}), .eq(comparator_27_eq));  // open: gt, lt
  Comparator #(.width(7)) comparator_28 (.a(Instruction[6:0]), .b(7'b0110011), .eq(comparator_28_eq));  // open: gt, lt
  Comparator #(.width(3)) comparator_29 (.a(Instruction[14:12]), .b(3'b101), .eq(comparator_29_eq));  // open: gt, lt
  Comparator #(.width(7)) comparator_30 (
    .a(Instruction[31:25]), .b(7'b0100000), .eq(comparator_30_eq));  // open: gt, lt
  Comparator #(.width(7)) comparator_31 (.a(Instruction[6:0]), .b(7'b0110011), .eq(comparator_31_eq));  // open: gt, lt
  Comparator #(.width(3)) comparator_32 (.a(Instruction[14:12]), .b(3'b110), .eq(comparator_32_eq));  // open: gt, lt
  Comparator #(.width(7)) comparator_33 (.a(Instruction[31:25]), .b({7{1'b0}}), .eq(comparator_33_eq));  // open: gt, lt
  Comparator #(.width(7)) comparator_34 (.a(Instruction[6:0]), .b(7'b0110011), .eq(comparator_34_eq));  // open: gt, lt
  Comparator #(.width(3)) comparator_35 (.a(Instruction[14:12]), .b(3'b111), .eq(comparator_35_eq));  // open: gt, lt
  Comparator #(.width(7)) comparator_36 (.a(Instruction[31:25]), .b({7{1'b0}}), .eq(comparator_36_eq));  // open: gt, lt
  Comparator #(.width(7)) comparator_37 (.a(Instruction[6:0]), .b(7'b0000011), .eq(comparator_37_eq));  // open: gt, lt
  Comparator #(.width(3)) comparator_38 (.a(Instruction[14:12]), .b(3'b000), .eq(comparator_38_eq));  // open: gt, lt
  Comparator #(.width(7)) comparator_39 (.a(Instruction[6:0]), .b(7'b0000011), .eq(comparator_39_eq));  // open: gt, lt
  Comparator #(.width(3)) comparator_40 (.a(Instruction[14:12]), .b(3'b001), .eq(comparator_40_eq));  // open: gt, lt
  Comparator #(.width(7)) comparator_41 (.a(Instruction[6:0]), .b(7'b0000011), .eq(comparator_41_eq));  // open: gt, lt
  Comparator #(.width(3)) comparator_42 (.a(Instruction[14:12]), .b(3'b010), .eq(comparator_42_eq));  // open: gt, lt
  Comparator #(.width(7)) comparator_43 (.a(Instruction[6:0]), .b(7'b0010011), .eq(comparator_43_eq));  // open: gt, lt
  Comparator #(.width(3)) comparator_44 (.a(Instruction[14:12]), .b(3'b000), .eq(comparator_44_eq));  // open: gt, lt
  Comparator #(.width(7)) comparator_45 (.a(Instruction[6:0]), .b(7'b0010011), .eq(comparator_45_eq));  // open: gt, lt
  Comparator #(.width(3)) comparator_46 (.a(Instruction[14:12]), .b(3'b001), .eq(comparator_46_eq));  // open: gt, lt
  Comparator #(.width(7)) comparator_47 (.a(Instruction[31:25]), .b({7{1'b0}}), .eq(comparator_47_eq));  // open: gt, lt
  Comparator #(.width(7)) comparator_48 (.a(Instruction[6:0]), .b(7'b0010011), .eq(comparator_48_eq));  // open: gt, lt
  Comparator #(.width(3)) comparator_49 (.a(Instruction[14:12]), .b(3'b010), .eq(comparator_49_eq));  // open: gt, lt
  Comparator #(.width(7)) comparator_50 (.a(Instruction[6:0]), .b(7'b0010011), .eq(comparator_50_eq));  // open: gt, lt
  Comparator #(.width(3)) comparator_51 (.a(Instruction[14:12]), .b(3'b100), .eq(comparator_51_eq));  // open: gt, lt
  Comparator #(.width(7)) comparator_52 (.a(Instruction[6:0]), .b(7'b0010011), .eq(comparator_52_eq));  // open: gt, lt
  Comparator #(.width(3)) comparator_53 (.a(Instruction[14:12]), .b(3'b101), .eq(comparator_53_eq));  // open: gt, lt
  Comparator #(.width(7)) comparator_54 (.a(Instruction[31:25]), .b({7{1'b0}}), .eq(comparator_54_eq));  // open: gt, lt
  Comparator #(.width(7)) comparator_55 (.a(Instruction[6:0]), .b(7'b0010011), .eq(comparator_55_eq));  // open: gt, lt
  Comparator #(.width(3)) comparator_56 (.a(Instruction[14:12]), .b(3'b101), .eq(comparator_56_eq));  // open: gt, lt
  Comparator #(.width(7)) comparator_57 (
    .a(Instruction[31:25]), .b(7'b0100000), .eq(comparator_57_eq));  // open: gt, lt
  Comparator #(.width(7)) comparator_58 (.a(Instruction[6:0]), .b(7'b0010011), .eq(comparator_58_eq));  // open: gt, lt
  Comparator #(.width(3)) comparator_59 (.a(Instruction[14:12]), .b(3'b110), .eq(comparator_59_eq));  // open: gt, lt
  Comparator #(.width(7)) comparator_60 (.a(Instruction[6:0]), .b(7'b0010011), .eq(comparator_60_eq));  // open: gt, lt
  Comparator #(.width(3)) comparator_61 (.a(Instruction[14:12]), .b(3'b111), .eq(comparator_61_eq));  // open: gt, lt
  Comparator #(.width(7)) comparator_62 (.a(Instruction[6:0]), .b(7'b0100011), .eq(comparator_62_eq));  // open: gt, lt
  Comparator #(.width(3)) comparator_63 (.a(Instruction[14:12]), .b(3'b000), .eq(comparator_63_eq));  // open: gt, lt
  Comparator #(.width(7)) comparator_64 (.a(Instruction[6:0]), .b(7'b0100011), .eq(comparator_64_eq));  // open: gt, lt
  Comparator #(.width(3)) comparator_65 (.a(Instruction[14:12]), .b(3'b001), .eq(comparator_65_eq));  // open: gt, lt
  Comparator #(.width(7)) comparator_66 (.a(Instruction[6:0]), .b(7'b0100011), .eq(comparator_66_eq));  // open: gt, lt
  Comparator #(.width(3)) comparator_67 (.a(Instruction[14:12]), .b(3'b010), .eq(comparator_67_eq));  // open: gt, lt
  Comparator #(.width(7)) comparator_68 (.a(Instruction[6:0]), .b(7'b1100011), .eq(comparator_68_eq));  // open: gt, lt
  Comparator #(.width(3)) comparator_69 (.a(Instruction[14:12]), .b(3'b000), .eq(comparator_69_eq));  // open: gt, lt
  Comparator #(.width(7)) comparator_70 (.a(Instruction[6:0]), .b(7'b1100011), .eq(comparator_70_eq));  // open: gt, lt
  Comparator #(.width(3)) comparator_71 (.a(Instruction[14:12]), .b(3'b001), .eq(comparator_71_eq));  // open: gt, lt
  Comparator #(.width(7)) comparator_72 (.a(Instruction[6:0]), .b(7'b1100011), .eq(comparator_72_eq));  // open: gt, lt
  Comparator #(.width(3)) comparator_73 (.a(Instruction[14:12]), .b(3'b100), .eq(comparator_73_eq));  // open: gt, lt
  Comparator #(.width(7)) comparator_74 (.a(Instruction[6:0]), .b(7'b1100011), .eq(comparator_74_eq));  // open: gt, lt
  Comparator #(.width(3)) comparator_75 (.a(Instruction[14:12]), .b(3'b101), .eq(comparator_75_eq));  // open: gt, lt
  Comparator #(.width(7)) comparator_76 (.a(Instruction[6:0]), .b(7'b1100011), .eq(comparator_76_eq));  // open: gt, lt
  Comparator #(.width(3)) comparator_77 (.a(Instruction[14:12]), .b(3'b110), .eq(comparator_77_eq));  // open: gt, lt
  Comparator #(.width(7)) comparator_78 (.a(Instruction[6:0]), .b(7'b1100011), .eq(comparator_78_eq));  // open: gt, lt
  Comparator #(.width(3)) comparator_79 (.a(Instruction[14:12]), .b(3'b111), .eq(comparator_79_eq));  // open: gt, lt
  Comparator #(.width(7)) comparator_80 (.a(Instruction[6:0]), .b(7'b0010111), .eq(is_auipc));  // open: gt, lt
  Comparator #(.width(7)) comparator_81 (.a(Instruction[6:0]), .b(7'b0110111), .eq(is_lui));  // open: gt, lt
  Comparator #(.width(7)) comparator_82 (.a(Instruction[6:0]), .b(7'b1101111), .eq(is_jal));  // open: gt, lt
  Comparator #(.width(7)) comparator_83 (.a(Instruction[6:0]), .b(7'b1100111), .eq(comparator_83_eq));  // open: gt, lt
  Comparator #(.width(3)) comparator_84 (.a(Instruction[14:12]), .b(3'b000), .eq(comparator_84_eq));  // open: gt, lt
  and and_1 (is_add, comparator_1_eq, comparator_2_eq, comparator_3_eq);
  and and_2 (is_mul, comparator_4_eq, comparator_5_eq, comparator_6_eq);
  and and_3 (is_sub, comparator_7_eq, comparator_8_eq, comparator_9_eq);
  and and_4 (is_sll, comparator_10_eq, comparator_11_eq, comparator_12_eq);
  and and_5 (is_mulh, comparator_13_eq, comparator_14_eq, comparator_15_eq);
  and and_6 (is_mulhu, comparator_16_eq, comparator_17_eq, comparator_18_eq);
  and and_7 (is_slt, comparator_19_eq, comparator_20_eq, comparator_21_eq);
  and and_8 (is_xor, comparator_22_eq, comparator_23_eq, comparator_24_eq);
  and and_9 (is_srl, comparator_25_eq, comparator_26_eq, comparator_27_eq);
  and and_10 (is_sra, comparator_28_eq, comparator_29_eq, comparator_30_eq);
  and and_11 (is_or, comparator_31_eq, comparator_32_eq, comparator_33_eq);
  and and_12 (is_and, comparator_34_eq, comparator_35_eq, comparator_36_eq);
  and and_13 (is_lb, comparator_37_eq, comparator_38_eq);
  and and_14 (is_lh, comparator_39_eq, comparator_40_eq);
  and and_15 (is_lw, comparator_41_eq, comparator_42_eq);
  and and_16 (is_addi, comparator_43_eq, comparator_44_eq);
  and and_17 (is_slli, comparator_45_eq, comparator_46_eq, comparator_47_eq);
  and and_18 (is_slti, comparator_48_eq, comparator_49_eq);
  and and_19 (is_xori, comparator_50_eq, comparator_51_eq);
  and and_20 (is_srli, comparator_52_eq, comparator_53_eq, comparator_54_eq);
  and and_21 (is_srai, comparator_55_eq, comparator_56_eq, comparator_57_eq);
  and and_22 (is_ori, comparator_58_eq, comparator_59_eq);
  and and_23 (is_andi, comparator_60_eq, comparator_61_eq);
  and and_24 (is_sb, comparator_62_eq, comparator_63_eq);
  and and_25 (is_sh, comparator_64_eq, comparator_65_eq);
  and and_26 (is_sw, comparator_66_eq, comparator_67_eq);
  and and_27 (is_beq, comparator_68_eq, comparator_69_eq);
  and and_28 (is_bne, comparator_70_eq, comparator_71_eq);
  and and_29 (is_blt, comparator_72_eq, comparator_73_eq);
  and and_30 (is_bge, comparator_74_eq, comparator_75_eq);
  and and_31 (is_bltu, comparator_76_eq, comparator_77_eq);
  and and_32 (is_bgeu, comparator_78_eq, comparator_79_eq);
  and and_33 (is_jalr, comparator_83_eq, comparator_84_eq);
  Priority_Encoder #(.select(4)) priority_encoder_1 (
    .in0(is_add), .in1(is_mul), .in2(is_sub), .in3(is_sll), .in4(is_mulh), .in5(is_mulhu), .in6(is_slt),
    .in7(is_xor), .in8(is_srl), .in9(is_sra), .in10(is_or), .in11(is_and), .in12(is_lb), .in13(is_lh),
    .in14(is_lw), .in15(is_addi), .out(priority_encoder_1_out), .gs(priority_encoder_1_gs));  // open: en_out, en_in
  Priority_Encoder #(.select(4)) priority_encoder_2 (
    .in0(is_slli), .in1(is_slti), .in2(is_xori), .in3(is_srli), .in4(is_srai), .in5(is_ori), .in6(is_andi),
    .in7(is_sb), .in8(is_sh), .in9(is_sw), .in10(is_beq), .in11(is_bne), .in12(is_blt), .in13(is_bge),
    .in14(is_bltu), .in15(is_bgeu), .out(priority_encoder_2_out), .gs(priority_encoder_2_gs));  // open: en_out, en_in
  Priority_Encoder #(.select(2)) priority_encoder_3 (
    .in0(is_auipc), .in1(is_lui), .in2(is_jal), .in3(is_jalr), .out(priority_encoder_3_out),
    .gs(priority_encoder_3_gs));  // open: en_out, en_in
  Multiplexer #(.enable("false"), .width(4)) multiplexer_1 (
    .in0(4'b0000), .in1(priority_encoder_1_out), .out(multiplexer_1_out), .sel(priority_encoder_1_gs));
  assign bit_extender_1_out = {{2{1'b0}}, priority_encoder_2_out};  // Bit_Extender bit_extender_1
  assign bit_extender_2_out = {{4{1'b0}}, priority_encoder_3_out};  // Bit_Extender bit_extender_2
  not not_1 (not_1_out, BrEq);
  assign bit_extender_3_out = {{2{1'b0}}, multiplexer_1_out};  // Bit_Extender bit_extender_3
  Adder #(.width(6)) adder_1 (.a(6'b010000), .b(bit_extender_1_out), .out(adder_1_out));  // open: cin, cout
  Adder #(.width(6)) adder_2 (.a(6'b100000), .b(bit_extender_2_out), .out(adder_2_out));  // open: cin, cout
  and and_34 (and_34_out, BrEq, is_beq);
  and and_35 (and_35_out, not_1_out, is_bne);
  and and_36 (and_36_out, BrLt, is_blt);
  not not_2 (not_2_out, BrLt);
  and and_37 (and_37_out, not_2_out, is_bge);
  and and_38 (and_38_out, BrLt, is_bltu);
  not not_3 (not_3_out, BrLt);
  and and_39 (and_39_out, not_3_out, is_bgeu);
  Multiplexer #(.enable("false"), .width(6)) multiplexer_2 (
    .in0({6{1'b0}}), .in1(adder_1_out), .out(multiplexer_2_out), .sel(priority_encoder_2_gs));
  Multiplexer #(.enable("false"), .width(6)) multiplexer_3 (
    .in0({6{1'b0}}), .in1(adder_2_out), .out(multiplexer_3_out), .sel(priority_encoder_3_gs));
  Adder #(.width(6)) adder_3 (.a(bit_extender_3_out), .b(multiplexer_2_out), .out(adder_3_out));  // open: cin, cout
  Adder #(.width(6)) adder_4 (.a(adder_3_out), .b(multiplexer_3_out), .out(out_13));  // open: cin, cout
  or or_1 (PCSel, and_34_out, and_35_out, and_36_out, and_37_out, and_38_out, and_39_out, is_jal, is_jalr);

  // Other names for the same wires on the sheet: opcode[6:0] = Instruction[6:0]; dontcare1[4:0] = Instruction[11:7];
  //   func3[2:0] = Instruction[14:12]; dontcare2[4:0] = Instruction[19:15]; dontcare3[4:0] = Instruction[24:20];
  //   func7[6:0] = Instruction[31:25]; rom_input[5:0] = out_13

  // Notes on the sheet:
  //   INPUTS to your circuit
  //   contents of rom_1 (hex, n*v repeats v):
  //   1001 1401 1601 1081 1481 1581 1101 1201 1281 1681 1301 1381 2041 2041 2041 1041 10c1 1141 1241 12c1
  //   16c1 1341 13c1 842 842 842 4*1064 1074 1074 1067 17c7 69 41
  //   ROM FOR CONTROL LOGIC
  //   DON'T CHANGE THE LOCATIONS OF THE INPUTS AND OUTPUTS!
  //   This is only if you choose to do the ROM option
  //   CONNECT
  //   USE
  //   ROM
  //   OUTPUT from your circuit
  //   Reminder: If using ROM, use combinational logic for PCSel
endmodule
