// Logisim project cpu.circ as structural Verilog: 1 circuit, main circuit cpu
module cpu (
  input  clk,
  input  [31:0] Instruction,
  input  [31:0] MemReadData,
  output [31:0] MemAddress,
  output [31:0] ProgramCounter,
  output [31:0] ra,
  output [31:0] sp,
  output [31:0] t0,
  output [31:0] t1,
  output [31:0] t2,
  output [31:0] s0,
  output [31:0] s1,
  output [31:0] a0,
  output [3:0] MemWriteMask,
  output [31:0] MemWriteData
);

  wire asel, breq, brlt, brun, bsel, memwen, pcsel, regwen;
  wire [1:0] wbsel;
  wire [2:0] func3, immsel;
  wire [3:0] alusel;
  wire [6:0] func7;
  wire [24:0] Instructionpost;
  wire [31:0] a, b, imm, memtoreg, multiplexer_1_out, multiplexer_2_out, multiplexer_3_out,
       multiplexer_4_out, multiplexer_5_out, pc4, pc4post, ProgramCounter2;

  Adder #(.width(32)) adder_1 (.a(ProgramCounter), .b(32'h4), .out(pc4));  // open: cin, cout
  Register #(.width(32)) PC (.D(multiplexer_1_out), .clk(clk), .Q(ProgramCounter));  // open: en, clr
  Multiplexer #(.enable("false"), .width(32)) multiplexer_1 (
    .in0(pc4), .in1(MemAddress), .out(multiplexer_1_out), .sel(pcsel));
  Register #(.width(32)) register_1 (.D(ProgramCounter), .clk(clk), .Q(ProgramCounter2));  // open: en, clr
  Register #(.width(32)) register_2 (.D(pc4), .clk(clk), .Q(pc4post));  // open: en, clr
  Multiplexer #(.enable("false"), .width(32)) multiplexer_2 (
    .in0(Instruction), .in1(32'h13), .out(multiplexer_2_out), .sel(pcsel));
  Register #(.width(32)) register_3 (
    .D(multiplexer_2_out), .clk(clk), .Q({func7, Instructionpost[24:15], func3, Instructionpost[11:0]}));  // open: en, clr
  Multiplexer #(.enable("false"), .select(2), .width(32)) multiplexer_3 (
    .in0(pc4post), .in1(MemAddress), .in2(memtoreg), .out(multiplexer_3_out), .sel(wbsel));  // open: in3
  control_logic control_logic_1 (
    .PCSel(pcsel), .RegWEn(regwen), .ImmSel(immsel), .BrUn(brun), .ASel(asel), .BSel(bsel), .ALUSel(alusel),
    .MemWEn(memwen), .WBSel(wbsel),
    .Instruction({func7, Instructionpost[24:15], func3, Instructionpost[11:0]}), .BrEq(breq), .BrLt(brlt));  // open: out_13
  regfile regfile_1 (
    .ReadIndex1(Instructionpost[19:15]), .ReadIndex2(Instructionpost[24:20]),
    .WriteIndex(Instructionpost[11:7]), .WriteData(multiplexer_3_out), .RegWEn(regwen), .clk(clk), .ra(ra),
    .sp(sp), .t0(t0), .t1(t1), .t2(t2), .s0(s0), .s1(s1), .a0(a0), .ReadData1(a), .ReadData2(b));
  imm_gen imm_gen_1 (
    .Instruction({func7, Instructionpost[24:15], func3, Instructionpost[11:0]}), .ImmSel(immsel),
    .Immediate(imm));
  Multiplexer #(.enable("false"), .width(32)) multiplexer_4 (
    .in0(a), .in1(ProgramCounter2), .out(multiplexer_4_out), .sel(asel));
  Multiplexer #(.enable("false"), .width(32)) multiplexer_5 (.in0(b), .in1(imm), .out(multiplexer_5_out), .sel(bsel));
  alu alu_1 (.ALUResult(MemAddress), .A(multiplexer_4_out), .B(multiplexer_5_out), .ALUSel(alusel));
  branch_comp branch_comp_1 (.BrData1(a), .BrData2(b), .BrUn(brun), .BrEq(breq), .BrLt(brlt));
  partial_store partial_store_1 (
    .Instruction({func7, Instructionpost[24:15], func3, Instructionpost[11:0]}), .MemAddress(MemAddress),
    .DataFromReg(b), .MemWEn(memwen), .MemWriteMask(MemWriteMask), .DataToMem(MemWriteData));
  partial_load partial_load_1 (
    .Instruction({func7, Instructionpost[24:15], func3, Instructionpost[11:0]}), .MemAddress(MemAddress),
    .DataFromMem(MemReadData), .DataToReg(memtoreg));

  // Other names for the same wires on the sheet: opcode[6:0] = Instructionpost[6:0]; rd[4:0] = Instructionpost[11:7];
  //   Instructionpost (some bits) = {func7, func3}; rs1[4:0] = Instructionpost[19:15];
  //   rs2[4:0] = Instructionpost[24:20]; writedata[31:0] = MemAddress

  // Notes on the sheet:
  //   To IMEM
  //   IMEM (do **NOT** move this)
  //   From IMEM
  //   Inputs/Outputs for testing. Do **NOT** move these.
  //   It is OK to move the PC, RegFile, ALU, MEM, Branch Comp, Imm Gen, Partial Load, Partial Store and Control Logic to wherever is most convenient for you when constructing your CPU, and to delete this text
  //   To DMEM
  //   DMEM (do **NOT** move this)
  //   From DMEM
endmodule
