// Logisim project partial-load.circ as structural Verilog: 1 circuit, main circuit partial_load
module partial_load (
  input  [31:0] Instruction,
  input  [31:0] MemAddress,
  input  [31:0] DataFromMem,
  output [31:0] DataToReg
);

  wire [4:0] bit_extender_1_out, pos;
  wire [7:0] shifter_3_out;
  wire [23:0] shifter_3_out_2;
  wire [31:0] and_1_out, bit_extender_2_out, bit_extender_3_out, multiplexer_1_out, shifter_2_out;

  assign bit_extender_1_out = {{3{1'b0}}, MemAddress[1:0]};  // Bit_Extender bit_extender_1
  Shifter #(.width(5)) shifter_1 (.in(bit_extender_1_out), .\dist (3'b011), .out(pos));
  Multiplexer #(.enable("false"), .select(2), .width(32)) multiplexer_1 (
    .in0(32'hff), .in1(32'hffff), .in2({32{1'b1}}), .out(multiplexer_1_out), .sel(Instruction[13:12]));  // open: in3
  Shifter #(.width(32)) shifter_2 (.in(multiplexer_1_out), .\dist (pos), .out(shifter_2_out));
  assign and_1_out = DataFromMem & shifter_2_out;  // AND_Gate and_1, 32 bits wide
  Shifter #(.shift("lr"), .width(32)) shifter_3 (.in(and_1_out), .\dist (pos), .out({shifter_3_out_2, shifter_3_out}));
  assign bit_extender_2_out = {{24{shifter_3_out[7]}}, shifter_3_out};  // Bit_Extender bit_extender_2
  assign bit_extender_3_out = {{16{shifter_3_out_2[7]}}, {shifter_3_out_2[7:0], shifter_3_out}};  // Bit_Extender bit_extender_3
  Multiplexer #(.enable("false"), .select(2), .width(32)) multiplexer_2 (
    .in0(bit_extender_2_out), .in1(bit_extender_3_out), .in2({shifter_3_out_2, shifter_3_out}),
    .out(DataToReg), .sel(Instruction[13:12]));  // open: in3

  // Other names for the same wires on the sheet: load_type[1:0] = Instruction[13:12]

  // Notes on the sheet:
  //   INPUTS to your circuit
  //   DON'T CHANGE THE LOCATIONS OF THE INPUTS AND OUTPUTS!
  //   OUTPUT from your circuit
endmodule
