// Logisim project partial-store.circ as structural Verilog: 1 circuit, main circuit partial_store
module partial_store (
  input  [31:0] Instruction,
  input  [31:0] MemAddress,
  input  [31:0] DataFromReg,
  input  MemWEn,
  output [3:0] MemWriteMask,
  output [31:0] DataToMem
);

  wire [3:0] multiplexer_3_out, multiplexer_4_out, multiplexer_5_out;
  wire [4:0] toshift;
  wire [31:0] bit_extender_1_out, bit_extender_2_out, shifter_1_out, shifter_2_out;

  assign bit_extender_1_out = {{24{1'b0}}, DataFromReg[7:0]};  // Bit_Extender bit_extender_1
  assign bit_extender_2_out = {{16{1'b0}}, DataFromReg[15:0]};  // Bit_Extender bit_extender_2
  Shifter #(.width(32)) shifter_1 (.in(bit_extender_1_out), .\dist (toshift), .out(shifter_1_out));
  Shifter #(.width(32)) shifter_2 (.in(bit_extender_2_out), .\dist (toshift), .out(shifter_2_out));
  Multiplexer #(.enable("false"), .select(2), .width(5)) multiplexer_1 (
    .in0({5{1'b0}}), .in1(5'b01000), .in2(5'b10000), .in3(5'b11000), .out(toshift), .sel(MemAddress[1:0]));
  Multiplexer #(.enable("false"), .select(2), .width(32)) multiplexer_2 (
    .in0(shifter_1_out), .in1(shifter_2_out), .in2(DataFromReg), .out(DataToMem), .sel(Instruction[13:12]));  // open: in3
  Multiplexer #(.enable("false"), .select(2), .width(4)) multiplexer_3 (
    .in0(4'b0001), .in1(4'b0010), .in2(4'b0100), .in3(4'b1000), .out(multiplexer_3_out));  // open: sel
  Multiplexer #(.enable("false"), .select(2), .width(4)) multiplexer_4 (
    .in0(4'b0011), .in2(4'b1100), .out(multiplexer_4_out));  // open: in1, in3, sel
  Multiplexer #(.enable("false"), .select(2), .width(4)) multiplexer_5 (
    .in0(multiplexer_3_out), .in1(multiplexer_4_out), .in2(4'b1111), .out(multiplexer_5_out));  // open: in3, sel
  Multiplexer #(.enable("false"), .width(4)) multiplexer_6 (
    .in0(4'b0000), .in1(multiplexer_5_out), .out(MemWriteMask), .sel(MemWEn));

  // Other names for the same wires on the sheet: storetype[1:0] = Instruction[13:12];
  //   bottombits[1:0] = MemAddress[1:0]

  // Notes on the sheet:
  //   INPUTS to your circuit
  //   DON'T CHANGE THE LOCATIONS OF THE INPUTS AND OUTPUTS!
  //   OUTPUT from your circuit
endmodule
